// Logisim project SomadorCompleto.circ as structural Verilog: 6 circuits, main circuit main
module main (
  input  [3:0] in_1,
  input  [3:0] in_2,
  output [3:0] out_3
);

  Somador_De_4_Bits somador_de_4_bits_1 (.A(in_1), .B(in_2), .Saida(out_3));  // open: Carry_Out
endmodule

module Meio_Somador (
  input  A0,
  input  B0,
  output Soma,
  output Carry_Out
);

  xor xor_1 (Soma, A0, B0);
  and and_1 (Carry_Out, A0, B0);
endmodule

module Somador_Completo__Abstraido (
  input  A,
  input  B,
  input  Ci,
  output Soma,
  output Co
);

  wire meio_somador_1_carry_out, meio_somador_1_soma, meio_somador_2_carry_out;

  Meio_Somador meio_somador_1 (.Soma(meio_somador_1_soma), .Carry_Out(meio_somador_1_carry_out), .A0(A), .B0(B));
  Meio_Somador meio_somador_2 (.Soma(Soma), .Carry_Out(meio_somador_2_carry_out), .A0(meio_somador_1_soma), .B0(Ci));
  or or_1 (Co, meio_somador_2_carry_out, meio_somador_1_carry_out);
endmodule

module Somador_Completo (
  input  Ci,
  input  A0,
  input  B0,
  output Soma,
  output Carry_Out,
  output Carry_Out_2,
  output Soma_2,
  output Carry_Out_3
);

  xor xor_1 (Soma, A0, B0);
  and and_1 (Carry_Out, A0, B0);
  xor xor_2 (Soma_2, Ci, Soma);
  and and_2 (Carry_Out_3, Ci, Soma);
  or or_1 (Carry_Out_2, Carry_Out, Carry_Out_3);
endmodule

module Somador_De_4_Bits (
  input  [3:0] A,
  input  [3:0] B,
  output [3:0] Saida,
  output Carry_Out
);

  wire somador_completo_abstraido_1_co, somador_completo_abstraido_2_co, somador_completo_abstraido_3_co;

  Somador_Completo__Abstraido somador_completo_abstraido_1 (
    .A(B[0]), .B(A[0]), .Ci(1'b0), .Soma(Saida[0]), .Co(somador_completo_abstraido_1_co));
  Somador_Completo__Abstraido somador_completo_abstraido_2 (
    .A(B[1]), .B(A[1]), .Ci(somador_completo_abstraido_1_co), .Soma(Saida[1]),
    .Co(somador_completo_abstraido_2_co));
  Somador_Completo__Abstraido somador_completo_abstraido_3 (
    .A(B[2]), .B(A[2]), .Ci(somador_completo_abstraido_2_co), .Soma(Saida[2]),
    .Co(somador_completo_abstraido_3_co));
  Somador_Completo__Abstraido somador_completo_abstraido_4 (
    .A(B[3]), .B(A[3]), .Ci(somador_completo_abstraido_3_co), .Soma(Saida[3]), .Co(Carry_Out));
endmodule

module Somador_Completo__Overflow (
  input  [3:0] A,
  input  [3:0] B,
  output [3:0] Saida,
  output Overflow,
  output Undeflow,
  output Carry_Out
);

  wire somador_completo_abstraido_1_co, somador_completo_abstraido_2_co, somador_completo_abstraido_3_co;

  Somador_Completo__Abstraido somador_completo_abstraido_1 (
    .A(B[0]), .B(A[0]), .Ci(1'b0), .Soma(Saida[0]), .Co(somador_completo_abstraido_1_co));
  Somador_Completo__Abstraido somador_completo_abstraido_2 (
    .A(B[1]), .B(A[1]), .Ci(somador_completo_abstraido_1_co), .Soma(Saida[1]),
    .Co(somador_completo_abstraido_2_co));
  Somador_Completo__Abstraido somador_completo_abstraido_3 (
    .A(B[2]), .B(A[2]), .Ci(somador_completo_abstraido_2_co), .Soma(Saida[2]),
    .Co(somador_completo_abstraido_3_co));
  Somador_Completo__Abstraido somador_completo_abstraido_4 (
    .A(B[3]), .B(A[3]), .Ci(somador_completo_abstraido_3_co), .Soma(Saida[3]), .Co(Carry_Out));
  and and_1 (Overflow, ~B[3], ~A[3], Saida[3]);  // AND_Gate
  and and_2 (Undeflow, B[3], A[3], ~Saida[3]);  // AND_Gate

  // Other names for the same wires on the sheet: _3 = B[3]
endmodule
